# Fritzing sketch robotics project (saved by Fritzing 0.9.3b)
breadboards: 1

parts:
  Soil_Mostuire_sensor = Soil Moisture Sensor
  Arduino = Arduino Uno (Rev3)
  Pizeo_Buzzer = Piezo Speaker
  LED1 = LED - 5mm [color="Red (633nm)" package="5 mm [THT]"]
  R1 = Resistor [tolerance=±5% resistance=220 package=THT]

nets:
  VCC: Soil_Mostuire_sensor.VCC, Arduino.5V
  N1: Soil_Mostuire_sensor.SIG, Arduino.A0
  GND: Soil_Mostuire_sensor.GND, Arduino.GND, Pizeo_Buzzer.pin1, LED1.cathode
  N2: Arduino.D11_PWM/MOSI, Pizeo_Buzzer.pin2
  N3: Arduino.D6_PWM, R1.Pin_1
  N4: LED1.anode, R1.Pin_0
